# Fritzing sketch motor_controllerfzz (saved by Fritzing 0.9.3b)
circuit board: 8.46667cm x 5.64444cm
perfboards: 1

parts:
  C1_FILT = Tantalum Capacitor [capacitance=100nF package="100 mil [THT, tantalum]"]
  C2_FILT = Tantalum Capacitor [capacitance=100nF package="100 mil [THT, tantalum]"]
  Rp = Resistor [tolerance=±5% resistance=100 package="0805 [SMD]"]
  D2 = Diode [package=diode-hv]
  D1 = Diode [package=diode-hv]
  Driver_IC = IC, DIP package, 20 pins [chip_label=L6205]
  V_&_GND = Camdenboss CTB0158-2 [part_number=CTB0158-2 package=THT]
  M2_OUT = Camdenboss CTB0158-2 [part_number=CTB0158-2 package=THT]
  M1_OUT = Camdenboss CTB0158-2 [part_number=CTB0158-2 package=THT]
  Cboot = Capacitor [package=cap-pth-small]
  M1_IO_&_SIG_GND = Camdenboss CTB0158-3 [part_number=CTB0158-3 package=THT]
  VDD_1 = Resistor [tolerance=±5% resistance=22k package=THT]
  VDD_2 = Resistor [tolerance=±10% resistance=15k package=THT]
  M2_IO = Camdenboss CTB0158-2 [part_number=CTB0158-2 package=THT]
  R_ENA = Resistor [tolerance=±5% resistance=10k package="0805 [SMD]"]
  C_ENA = Ceramic Capacitor [capacitance=100nF package="100 mil [THT, multilayer]"]
  Cp = Capacitor [package=cap-pth-5mm]

nets:
  N1: C1_FILT.-, C2_FILT.-, Driver_IC.pin3, Driver_IC.pin5, Driver_IC.pin6, Driver_IC.pin8, Driver_IC.pin15, Driver_IC.pin16, V_&_GND.pin2, M1_IO_&_SIG_GND.pin1, VDD_2.Pin_0, C_ENA.0
  N2: C1_FILT.+, C2_FILT.+, D1.A, Driver_IC.pin14, Driver_IC.pin17, V_&_GND.pin1, Cboot.1, VDD_1.Pin_1
  N3: Rp.Pin_0, D2.A, D1.C
  N4: Rp.Pin_1, Cp.1
  N5: D2.C, Driver_IC.pin12, Cboot.2
  N6: Driver_IC.pin1, M1_IO_&_SIG_GND.pin3
  N7: Driver_IC.pin2, M1_IO_&_SIG_GND.pin2
  N8: Driver_IC.pin4, M1_OUT.pin2
  N9: Driver_IC.pin7, M2_OUT.pin2
  N10: Driver_IC.pin9, M2_IO.pin2
  N11: Driver_IC.pin10, M2_IO.pin1
  N12: Driver_IC.pin11, Driver_IC.pin20, R_ENA.Pin_0, C_ENA.1
  N13: Driver_IC.pin13, M2_OUT.pin1
  N14: Driver_IC.pin18, M1_OUT.pin1
  N15: Driver_IC.pin19, Cp.2
  12V: V_&_GND.terminal_1
  GND: V_&_GND.terminal_2
  N16: VDD_1.Pin_0, VDD_2.Pin_1, R_ENA.Pin_1

notes:
  Voltage Divider ~4.58 V Enable Pin HIGH
  Bootstrapping Voltage Charge Pump
  Microcontroller Input
  M1_IO:
  IN1A,IN2A, Signal Ground
  M2_IO:
  IN1B, IN2B
  12V Input from buck converter
  Motor Output
  M1_OUT:
  OUT1A, OUT2A
  M2_OUT:
  OUT1B, OUT2B
